# Fritzing sketch p1_2021-22 (saved by Fritzing 0.9.9b)
breadboards: 1

parts:
  Mod1 = Raspberry Pi 4B
  Köz_Piros = LED - 5mm [color="Red (633nm)" current=0.030 package="5 mm [THT]"]
  Köz_Sárga = LED - 5mm [color="Yellow (585nm)" current=0.030 package="5 mm [THT]"]
  Köz_Zöld = LED - 5mm [color="Green (555nm)" current=0.030 package="5 mm [THT]"]
  Gyalog_Piros = LED - 5mm [color="Red (633nm)" current=0.030 package="5 mm [THT]"]
  Gyalog_Zöld = LED - 5mm [color="Green (555nm)" current=0.030 package="5 mm [THT]"]
  R1 = Resistor [tolerance=±5% power=0.25 resistance=470 package=THT]
  R5 = Resistor [tolerance=±5% power=0.25 resistance=470 package=THT]
  R6 = Resistor [tolerance=±5% power=0.25 resistance=470 package=THT]
  R7 = Resistor [tolerance=±5% power=0.25 resistance=470 package=THT]
  R8 = Resistor [tolerance=±5% power=0.25 resistance=470 package=THT]

nets:
  N1: Mod1.GPIO13, R5.Pin_1
  N2: Mod1.GPIO16, R8.Pin_1
  N3: Mod1.GPIO26, R1.Pin_1
  N4: Mod1.GPIO20, R7.Pin_1
  N5: Mod1.GND, Köz_Piros.cathode, Köz_Sárga.cathode, Köz_Zöld.cathode, Gyalog_Piros.cathode, Gyalog_Zöld.cathode
  N6: Mod1.GPIO21, R6.Pin_1
  N7: Köz_Piros.anode, R6.Pin_0
  N8: Köz_Sárga.anode, R7.Pin_0
  N9: Köz_Zöld.anode, R8.Pin_0
  N10: Gyalog_Piros.anode, R1.Pin_0
  N11: Gyalog_Zöld.anode, R5.Pin_0
